// Logisim project ProjetoULA_Ana_Rosa_15.circ as structural Verilog
module main (
  input  [7:0] A,
  input  [7:0] B,
  input  [3:0] OPCODE,
  input  [2:0] in_4,
  output [7:0] SAIDA
);

  wire [7:0] deslocd_1_out_3, desloce_1_out_3, E_out, INVERSORA_out, multiplier_1_out, NAO_E_out,
       NAO_OU_EXCLUSIVO_out, NAO_OU_out, OU_EXCLUSIVO_out, OU_out, som8_1_out_4, sub8_1_out_4;

  assign E_out = A & B;  // AND_Gate E, 8 bits wide
  assign OU_out = A | B;  // OR_Gate OU, 8 bits wide
  assign INVERSORA_out = ~B;  // NOT_Gate INVERSORA, 8 bits wide
  assign OU_EXCLUSIVO_out = A ^ B;  // XOR_Gate OU_EXCLUSIVO, 8 bits wide
  assign NAO_OU_out = ~(A | B);  // NOR_Gate NAO_OU, 8 bits wide
  assign NAO_E_out = ~(A & B);  // NAND_Gate NAO_E, 8 bits wide
  Multiplier multiplier_1 (.a(A), .b(B), .out(multiplier_1_out));  // open: cin, cout
  som8 som8_1 (.in_1(A), .in_2(B), .out_4(som8_1_out_4));  // open: out_3
  sub8 sub8_1 (.in_1(A), .in_2(B), .out_4(sub8_1_out_4));  // open: out_3
  assign NAO_OU_EXCLUSIVO_out = ~(A ^ B);  // XNOR_Gate NAO_OU_EXCLUSIVO, 8 bits wide
  deslocE desloce_1 (.in_1(B), .in_2(in_4), .out_3(desloce_1_out_3));
  deslocD deslocd_1 (.in_1(B), .in_2(in_4), .out_3(deslocd_1_out_3));
  Multiplexer #(.select(4), .width(8), .enable("false")) multiplexer_1 (
    .in1(NAO_OU_out), .in2(INVERSORA_out), .in3({8{1'b0}}), .in4(NAO_E_out), .in5(deslocd_1_out_3),
    .in6({8{1'b0}}), .in7(OU_EXCLUSIVO_out), .in8(multiplier_1_out), .in9(E_out), .in10(desloce_1_out_3),
    .in11(NAO_OU_EXCLUSIVO_out), .in12(som8_1_out_4), .in13({8{1'b0}}), .in14(OU_out), .in15(sub8_1_out_4),
    .out(SAIDA), .sel(OPCODE));  // open: in0
endmodule

module Somador (
  input  A,
  input  B,
  input  Carry_In,
  output Soma,
  output Carry_Out
);

  wire meiosom_1_out_3, meiosom_1_out_4, meiosom_2_out_4;

  meioSom meiosom_1 (.in_1(A), .in_2(B), .out_3(meiosom_1_out_3), .out_4(meiosom_1_out_4));
  meioSom meiosom_2 (.in_1(meiosom_1_out_3), .in_2(Carry_In), .out_3(Soma), .out_4(meiosom_2_out_4));
  or or_1 (Carry_Out, meiosom_2_out_4, meiosom_1_out_4);

  // Notes on the sheet:
  //   Carry
  //   Soma
  //   Carry
endmodule

module meioSub (
  input  in_1,
  input  in_2,
  output out_3,
  output out_4
);

  wire not_1_out;

  Multiplier multiplier_1 ();  // open: a, b, out, cin, cout
  not not_1 (not_1_out, in_1);
  xor xor_1 (out_3, in_1, in_2);
  and and_1 (out_4, in_2, not_1_out);
endmodule

module Subtrator (
  input  in_1,
  input  in_2,
  input  Borrow_In,
  output \Subtração ,
  output Borrow_Out
);

  wire meiosub_1_out_3, meiosub_1_out_4, meiosub_2_out_4;

  meioSub meiosub_1 (.in_1(in_1), .in_2(in_2), .out_3(meiosub_1_out_3), .out_4(meiosub_1_out_4));
  meioSub meiosub_2 (.in_1(meiosub_1_out_3), .in_2(Borrow_In), .out_3(\Subtração ), .out_4(meiosub_2_out_4));
  or or_1 (Borrow_Out, meiosub_2_out_4, meiosub_1_out_4);

  // Notes on the sheet:
  //   Subtração
  //   Borrow
  //   Borrow
endmodule

module meioSom (
  input  in_1,
  input  in_2,
  output out_3,
  output out_4
);

  xor xor_1 (out_3, in_2, in_1);
  and and_1 (out_4, in_1, in_2);
endmodule

module som8 (
  input  [7:0] in_1,
  input  [7:0] in_2,
  output out_3,
  output [7:0] out_4
);

  wire somador_2_carry_out, somador_3_carry_out, somador_4_carry_out, somador_5_carry_out,
       somador_6_carry_out, somador_7_carry_out, somador_8_carry_out, undriven;

  Somador somador_1 (.A(in_1[7]), .B(in_2[7]), .Carry_In(somador_2_carry_out), .Soma(out_4[7]), .Carry_Out(out_3));
  Somador somador_2 (
    .A(in_1[6]), .B(in_2[6]), .Carry_In(somador_3_carry_out), .Soma(out_4[6]), .Carry_Out(somador_2_carry_out));
  Somador somador_3 (
    .A(in_1[5]), .B(in_2[5]), .Carry_In(somador_4_carry_out), .Soma(out_4[5]), .Carry_Out(somador_3_carry_out));
  Somador somador_4 (
    .A(in_1[4]), .B(in_2[4]), .Carry_In(somador_5_carry_out), .Soma(out_4[4]), .Carry_Out(somador_4_carry_out));
  Somador somador_5 (
    .A(in_1[3]), .B(in_2[3]), .Carry_In(somador_6_carry_out), .Soma(out_4[3]), .Carry_Out(somador_5_carry_out));
  Somador somador_6 (
    .A(in_1[2]), .B(in_2[2]), .Carry_In(somador_7_carry_out), .Soma(out_4[2]), .Carry_Out(somador_6_carry_out));
  Somador somador_7 (
    .A(in_1[1]), .B(in_2[1]), .Carry_In(somador_8_carry_out), .Soma(out_4[1]), .Carry_Out(somador_7_carry_out));
  Somador somador_8 (.A(in_1[0]), .B(in_2[0]), .Carry_In(undriven), .Soma(out_4[0]), .Carry_Out(somador_8_carry_out));
endmodule

module sub8 (
  input  [7:0] in_1,
  input  [7:0] in_2,
  output out_3,
  output [7:0] out_4
);

  wire meiosub_1_out_4, subtrator_2_borrow_out, subtrator_3_borrow_out, subtrator_4_borrow_out,
       subtrator_5_borrow_out, subtrator_6_borrow_out, subtrator_7_borrow_out;

  Subtrator subtrator_1 (
    .in_1(in_1[7]), .in_2(in_2[7]), .Borrow_In(subtrator_2_borrow_out), .\Subtração (out_4[7]),
    .Borrow_Out(out_3));
  Subtrator subtrator_2 (
    .in_1(in_1[6]), .in_2(in_2[6]), .Borrow_In(subtrator_3_borrow_out), .\Subtração (out_4[6]),
    .Borrow_Out(subtrator_2_borrow_out));
  Subtrator subtrator_3 (
    .in_1(in_1[5]), .in_2(in_2[5]), .Borrow_In(subtrator_4_borrow_out), .\Subtração (out_4[5]),
    .Borrow_Out(subtrator_3_borrow_out));
  Subtrator subtrator_4 (
    .in_1(in_1[4]), .in_2(in_2[4]), .Borrow_In(subtrator_5_borrow_out), .\Subtração (out_4[4]),
    .Borrow_Out(subtrator_4_borrow_out));
  Subtrator subtrator_5 (
    .in_1(in_1[3]), .in_2(in_2[3]), .Borrow_In(subtrator_6_borrow_out), .\Subtração (out_4[3]),
    .Borrow_Out(subtrator_5_borrow_out));
  Subtrator subtrator_6 (
    .in_1(in_1[2]), .in_2(in_2[2]), .Borrow_In(subtrator_7_borrow_out), .\Subtração (out_4[2]),
    .Borrow_Out(subtrator_6_borrow_out));
  Subtrator subtrator_7 (
    .in_1(in_1[1]), .in_2(in_2[1]), .Borrow_In(meiosub_1_out_4), .\Subtração (out_4[1]),
    .Borrow_Out(subtrator_7_borrow_out));
  meioSub meiosub_1 (.in_1(in_1[0]), .in_2(in_2[0]), .out_3(out_4[0]), .out_4(meiosub_1_out_4));
endmodule

module deslocE (
  input  [7:0] in_1,
  input  [2:0] in_2,
  output [7:0] out_3
);

  Shifter shifter_1 (.in(in_1), .\dist (in_2), .out(out_3));
endmodule

module deslocD (
  input  [7:0] in_1,
  input  [2:0] in_2,
  output [7:0] out_3
);

  Shifter #(.shift("lr")) shifter_1 (.in(in_1), .\dist (in_2), .out(out_3));
endmodule
